# Fritzing sketch level_converter_circuit (saved by Fritzing 0.9.2b)
breadboards: 1

parts:
  C1 = Ceramic Capacitor [capacitance=100nF package="100 mil [THT, multilayer]"]
  Clk_in_out = Screw terminal - 2 pins [package=THT]
  Data_in_out = Screw terminal - 2 pins [package=THT]
  +5V_GND = Screw terminal - 2 pins [package=THT]
  74HC125N = IC, DIP package, 14 pins [chip_label=74HC125N part_number=74HC125N]
  Raspberry_Pi1 = Raspberry Pi 2

nets:
  N1: C1.0, +5V_GND.pin1, 74HC125N.pin1, 74HC125N.pin4, 74HC125N.pin7
  N2: C1.1, +5V_GND.pin2, 74HC125N.pin14
  N3: Clk_in_out.pin1, 74HC125N.pin3
  N4: Clk_in_out.pin2, 74HC125N.pin2, Raspberry_Pi1.GPIO11
  N5: Data_in_out.pin1, 74HC125N.pin6
  N6: Data_in_out.pin2, 74HC125N.pin5, Raspberry_Pi1.GPIO10
