# Fritzing sketch power-level_circuit (saved by Fritzing 0.9.2b)
breadboards: 1

parts:
  C1 = Ceramic Capacitor [capacitance=100nF package="100 mil [THT, multilayer]"]
  74HC125N = IC, DIP package, 14 pins [chip_label=74HC125N part_number=74HC125N]
  J1 = female pin header, 1 pin [form="♀ (female)"]
  J2 = female pin header, 1 pin [form="♀ (female)"]
  U1 = attiny85 [package=dip]
  Q1 = Basic FET P-Channel [package="TO220 [THT]"]
  R1 = Resistor [tolerance=±5% resistance=100k package=THT]
  C2 = Ceramic Capacitor [capacitance=10nF package="100 mil [THT, multilayer]"]
  J9 = Screw terminal - 2 pins [package=THT]
  J10 = Screw terminal - 2 pins [package=THT]
  J11 = Screw terminal - 2 pins [package=THT]
  J12 = Screw terminal - 2 pins [package=THT]
  R3 = Resistor [tolerance=±5% resistance=10k package=THT]
  R4 = Resistor [tolerance=±5% resistance=33k package=THT]
  R5 = Resistor [tolerance=±5% resistance=18k package=THT]
  J13 = Screw terminal - 2 pins [package=THT]
  R7 = Resistor [tolerance=±5% resistance=10k package=THT]
  J14 = female pin header, 1 pin [form="♀ (female)"]

nets:
  N1: C1.0, 74HC125N.pin1, 74HC125N.pin4, 74HC125N.pin7
  N2: C1.1, 74HC125N.pin14, J1.pin1, U1.Pin_8, J12.pin1
  N3: 74HC125N.pin2, J9.pin1
  N4: 74HC125N.pin3, J9.pin2
  N5: 74HC125N.pin5, J10.pin1
  N6: 74HC125N.pin6, J10.pin2
  N7: 74HC125N.pin10, Q1.drain, C2.0, J14.pin1
  N8: J2.pin1, U1.Pin_4, Q1.source, R4.Pin_0
  N9: U1.Pin_1, J12.pin2, R3.Pin_0
  N10: U1.Pin_2, R3.Pin_1
  N11: U1.Pin_3, R1.Pin_0
  N12: U1.Pin_5, J13.pin2
  N13: U1.Pin_6, R5.Pin_0
  N14: U1.Pin_7, R7.Pin_0
  N15: Q1.gate, R1.Pin_1, C2.1
  N16: J11.pin1, R7.Pin_1
  N17: J11.pin2, R4.Pin_1, R5.Pin_1
