# Fritzing sketch power-circuit (saved by Fritzing 0.8.5b)
breadboards: 1

parts:
  C1 = Ceramic Capacitor [capacitance=100nF package="100 mil [THT, multilayer]"]
  74HC125N = IC, DIP package, 14 pins [chip_label=74HC125N part_number=74HC125N]
  J1 = female pin header, 1 pin [form="♀ (female)"]
  J2 = female pin header, 1 pin [form="♀ (female)"]
  U1 = attiny85 [package=dip]
  Q1 = Basic FET P-Channel [package="TO220 [THT]"]
  R1 = Resistor [tolerance=±5% resistance=100k package=THT]
  C2 = Ceramic Capacitor [capacitance=10nF package="100 mil [THT, multilayer]"]
  Clk_in_out = Screw terminal - 2 pins [package=THT]
  Data_in_out = Screw terminal - 2 pins [package=THT]
  Btn_out_(5V)_Btn_in = Screw terminal - 2 pins [package=THT]
  R3 = Resistor [tolerance=±5% resistance=10k package=THT]
  R4 = Resistor [tolerance=±5% resistance=33k package=THT]
  R5 = Resistor [tolerance=±5% resistance=18k package=THT]
  R7 = Resistor [tolerance=±5% resistance=10k package=THT]
  J14 = female pin header, 1 pin [form="♀ (female)"]
  Btn_LED_Pw_in_out = screw terminal, 4 pins
  J15 = female pin header, 1 pin [form="♀ (female)"]

nets (from the breadboard view):
  N1: C1.0, 74HC125N.pin1, 74HC125N.pin4, 74HC125N.pin7, U1.Pin_4, R3.Pin_0, R4.Pin_0, Btn_LED_Pw_in_out.pin1
  N2: C1.1, 74HC125N.pin10, 74HC125N.pin11, 74HC125N.pin13, 74HC125N.pin14, J1.pin1, U1.Pin_8, Btn_out_(5V)_Btn_in.pin1, J15.pin1
  N3: 74HC125N.pin2, Clk_in_out.pin1
  N4: 74HC125N.pin3, Clk_in_out.pin2
  N5: 74HC125N.pin5, Data_in_out.pin1
  N6: 74HC125N.pin6, Data_in_out.pin2
  N7: 74HC125N.pin9, Q1.drain, C2.0, J14.pin1
  N8: J2.pin1, Q1.source
  N9: U1.Pin_2, Btn_out_(5V)_Btn_in.pin2, R3.Pin_1
  N10: U1.Pin_3, R1.Pin_0
  N11: U1.Pin_5, Btn_LED_Pw_in_out.pin2
  N12: U1.Pin_6, R5.Pin_0
  N13: U1.Pin_7, R7.Pin_0
  N14: Q1.gate, R1.Pin_1, C2.1
  N15: R4.Pin_1, R5.Pin_1, Btn_LED_Pw_in_out.pin4
  N16: R7.Pin_1, Btn_LED_Pw_in_out.pin3
